// Digital circuit UTS_1_1.dig as structural Verilog
module UTS_1_1 (
  input  a,
  input  c,
  input  b
);

  wire and_1_out, and_2_out, and_3_out, and_4_out, and_5_out, not_1_out, or_1_out, or_2_out, or_3_out;

  and and_1 (and_1_out, a, b);
  and and_2 (and_2_out, a, c);
  and and_3 (and_3_out, b, c);
  or or_1 (or_1_out, a, b, c);
  and and_4 (and_4_out, a, b, c);
  or or_2 (or_2_out, and_1_out, and_2_out, and_3_out);
  not not_1 (not_1_out, or_2_out);
  and and_5 (and_5_out, not_1_out, or_1_out);
  or or_3 (or_3_out, and_5_out, and_4_out);
  LED x (.in(or_3_out));

  // Notes on the sheet:
  //   (AB + AC + BC)' (A + B + C) + ABC
  //   UTS RANGKAIAN DIGITAL
  //   213050034 | MUHAMMAD JAMIL YUSUF
endmodule
