// Digital circuit UTS_1_10.dig as structural Verilog
module UTS_1_10 (
  input  W,
  input  X,
  input  Y,
  input  Z
);

  wire and_1_out, and_2_out, and_3_out, and_4_out, and_5_out, or_1_out;

  and and_1 (and_1_out, W, X, Y);
  and and_2 (and_2_out, W, ~X, Y);  // And
  and and_3 (and_3_out, W, X, Y, Z);
  and and_4 (and_4_out, W, ~X);  // And
  and and_5 (and_5_out, ~W, Y, ~Z);  // And
  or or_1 (or_1_out, and_1_out, and_2_out, and_3_out, and_4_out, and_5_out);
  LED a (.in(or_1_out));

  // Notes on the sheet:
  //   WXYZ + WX' + WX'Y + WXY + W'YZ'
  //   UTS RANGKAIAN DIGITAL
  //   213050034 | MUHAMMAD JAMIL YUSUF
endmodule
