// Digital circuit UTS_1_11.dig as structural Verilog
module UTS_1_11 (
  input  X,
  input  Y,
  input  Z
);

  wire and_1_out, and_2_out, and_3_out, and_4_out, or_1_out;

  and and_1 (and_1_out, X, Y);
  and and_2 (and_2_out, ~X, Y, Z);  // And
  and and_3 (and_3_out, ~X, ~Y, Z);  // And
  and and_4 (and_4_out, X, Y, ~Z);  // And
  or or_1 (or_1_out, and_1_out, and_2_out, and_3_out, and_4_out);
  LED A (.in(or_1_out));

  // Notes on the sheet:
  //   UTS RANGKAIAN DIGITAL
  //   213050034 | MUHAMMAD JAMIL YUSUF
  //   X'Y'Z + XYZ' + X'YZ + XY
endmodule
