// Digital circuit UTS_1_14.dig as structural Verilog
module UTS_1_14 (
  input  x,
  input  y,
  input  z
);

  wire and_1_out, and_2_out, and_3_out, and_4_out, or_1_out;

  and and_1 (and_1_out, ~x, y);  // And
  and and_2 (and_2_out, ~x, z);  // And
  and and_3 (and_3_out, x, ~z);  // And
  and and_4 (and_4_out, x, ~y);  // And
  or or_1 (or_1_out, and_1_out, and_2_out, and_3_out, and_4_out);
  LED a (.in(or_1_out));

  // Notes on the sheet:
  //   UTS RANGKAIAN DIGITAL
  //   213050034 | MUHAMMAD JAMIL YUSUF
  //   xz' + x'z + x'y + xy'
endmodule
