// Digital circuit UTS_1_2.dig as structural Verilog
module UTS_1_2 (
  input  a,
  input  b,
  input  c,
  input  d
);

  wire and_1_out, and_2_out, and_3_out, and_4_out, and_5_out, and_6_out, or_1_out;

  and and_1 (and_1_out, ~a, ~b, ~c);  // And
  and and_2 (and_2_out, ~a, c, d);  // And
  and and_3 (and_3_out, a, b, c);
  and and_4 (and_4_out, a, ~b, c);  // And
  and and_5 (and_5_out, ~a, b, d);  // And
  and and_6 (and_6_out, ~a, ~c, ~d);  // And
  or or_1 (or_1_out, and_1_out, and_2_out, and_3_out, and_4_out, and_5_out, and_6_out);
  LED x (.in(or_1_out));

  // Notes on the sheet:
  //   A'B'C' + A'CD + A'C'D' + A'BD + ABC + AB'C
  //   UTS RANGKAIAN DIGITAL
  //   213050034 | MUHAMMAD JAMIL YUSUF
endmodule
