// Digital circuit UTS_1_4.dig as structural Verilog
module UTS_1_4 (
  input  A,
  input  B,
  input  C,
  input  D
);

  wire and_1_out, and_2_out, and_3_out, or_1_out;

  and and_1 (and_1_out, ~A, B);  // And
  and and_2 (and_2_out, ~A, ~B, C);  // And
  and and_3 (and_3_out, C, D);
  or or_1 (or_1_out, and_1_out, and_2_out, and_3_out);
  LED X (.in(or_1_out));

  // Notes on the sheet:
  //   UTS RANGKAIAN DIGITAL
  //   213050034 | MUHAMMAD JAMIL YUSUF
  //   A'B + A'B'C + CD
endmodule
