// Digital circuit UTS_1_7.dig as structural Verilog
module UTS_1_7 (
  input  X,
  input  W,
  input  Y,
  input  Z
);

  wire and_1_out, and_2_out, and_3_out, and_4_out, or_1_out;

  and and_1 (and_1_out, ~W, X);  // And
  and and_2 (and_2_out, W, X, Y);
  and and_3 (and_3_out, ~W, ~X, Z);  // And
  and and_4 (and_4_out, X, ~Y);  // And
  or or_1 (or_1_out, and_1_out, and_2_out, and_3_out, and_4_out);
  LED led_1 (.in(or_1_out));

  // Notes on the sheet:
  //   UTS RANGKAIAN DIGITAL
  //   213050034 | MUHAMMAD JAMIL YUSUF
  //   W'X'Z + XY' + W'X + WXY
endmodule
